// Logisim project homework1.circ as structural Verilog: 3 circuits, main circuit main
module main (
  input  [7:0] in_1,
  input  DECREMENT,
  input  INCREMENT,
  input  LOAD
);

  wire CLOCK_out;
  wire [7:0] operation_1_output;

  Clock CLOCK (.out(CLOCK_out));
  Operation operation_1 (
    .\input (in_1), .DECREMENT(DECREMENT), .INCREMENT(INCREMENT), .clock(CLOCK_out), .Load(LOAD),
    .\output (operation_1_output));
  Hex_Digit_Display hex_digit_display_1 (.value(operation_1_output[7:4]));  // open: dp
  Hex_Digit_Display hex_digit_display_2 (.value(operation_1_output[3:0]));  // open: dp

  // Notes on the sheet:
  //   Resul Akçakaya 150119663
  //   Hamza Kavak 150118886
endmodule

module Register (
  input  in_1,
  input  in_2,
  input  in_3,
  input  in_4,
  input  in_5,
  input  in_6,
  input  in_7,
  input  in_8,
  input  in_9,
  input  LOAD,
  output out_11,
  output out_12,
  output out_13,
  output out_14,
  output out_15,
  output out_16,
  output out_17,
  output out_18
);

  wire and_1_out, and_2_out, and_3_out, and_4_out, and_5_out, and_6_out, and_7_out, and_8_out, and_9_out,
       and_10_out, and_11_out, and_12_out, and_13_out, and_14_out, and_15_out, and_16_out, not_1_out,
       not_2_out, not_3_out, not_4_out, not_5_out, not_6_out, not_7_out, not_8_out;

  not not_1 (not_1_out, in_1);
  not not_2 (not_2_out, in_2);
  not not_3 (not_3_out, in_3);
  not not_4 (not_4_out, in_4);
  not not_5 (not_5_out, in_5);
  not not_6 (not_6_out, in_6);
  not not_7 (not_7_out, in_7);
  not not_8 (not_8_out, in_8);
  and and_1 (and_1_out, in_1, LOAD);
  and and_2 (and_2_out, not_1_out, LOAD);
  and and_3 (and_3_out, in_2, LOAD);
  and and_4 (and_4_out, not_2_out, LOAD);
  and and_5 (and_5_out, in_3, LOAD);
  and and_6 (and_6_out, not_3_out, LOAD);
  and and_7 (and_7_out, in_4, LOAD);
  and and_8 (and_8_out, not_4_out, LOAD);
  and and_9 (and_9_out, in_5, LOAD);
  and and_10 (and_10_out, not_5_out, LOAD);
  and and_11 (and_11_out, in_6, LOAD);
  and and_12 (and_12_out, not_6_out, LOAD);
  and and_13 (and_13_out, in_7, LOAD);
  and and_14 (and_14_out, not_7_out, LOAD);
  and and_15 (and_15_out, in_8, LOAD);
  and and_16 (and_16_out, not_8_out, LOAD);
  S_R_Flip_Flop s_r_ff_1 (.S(and_1_out), .clk(in_9), .R(and_2_out), .Q(out_11));  // open: Qn, preset, reset, en
  S_R_Flip_Flop s_r_ff_2 (.S(and_3_out), .clk(in_9), .R(and_4_out), .Q(out_12));  // open: Qn, preset, reset, en
  S_R_Flip_Flop s_r_ff_3 (.S(and_5_out), .clk(in_9), .R(and_6_out), .Q(out_13));  // open: Qn, preset, reset, en
  S_R_Flip_Flop s_r_ff_4 (.S(and_7_out), .clk(in_9), .R(and_8_out), .Q(out_14));  // open: Qn, preset, reset, en
  S_R_Flip_Flop s_r_ff_5 (.S(and_9_out), .clk(in_9), .R(and_10_out), .Q(out_15));  // open: Qn, preset, reset, en
  S_R_Flip_Flop s_r_ff_6 (.S(and_11_out), .clk(in_9), .R(and_12_out), .Q(out_16));  // open: Qn, preset, reset, en
  S_R_Flip_Flop s_r_ff_7 (.S(and_13_out), .clk(in_9), .R(and_14_out), .Q(out_17));  // open: Qn, preset, reset, en
  S_R_Flip_Flop s_r_ff_8 (.S(and_15_out), .clk(in_9), .R(and_16_out), .Q(out_18));  // open: Qn, preset, reset, en

  // Notes on the sheet:
  //   We designed 8 bit register with using S-R FF for 8 bit input
endmodule

module Operation (
  input  [7:0] \input ,
  input  DECREMENT,
  input  Load,
  input  INCREMENT,
  input  clock,
  output [7:0] \output 
);

  wire or_1_out;
  wire [7:0] adder_1_out, multiplexer_1_out, subtractor_1_out;

  Multiplexer #(.select(2), .width(8), .enable("false")) multiplexer_1 (
    .in0(\input ), .in1(adder_1_out), .in2(subtractor_1_out), .in3(\output ), .out(multiplexer_1_out),
    .sel({DECREMENT, INCREMENT}));
  Register register_1 (
    .in_1(multiplexer_1_out[0]), .in_2(multiplexer_1_out[1]), .in_3(multiplexer_1_out[2]),
    .in_4(multiplexer_1_out[3]), .in_5(multiplexer_1_out[4]), .in_6(multiplexer_1_out[5]),
    .in_7(multiplexer_1_out[6]), .in_8(multiplexer_1_out[7]), .in_9(clock), .LOAD(or_1_out),
    .out_11(\output [0]), .out_12(\output [1]), .out_13(\output [2]), .out_14(\output [3]),
    .out_15(\output [4]), .out_16(\output [5]), .out_17(\output [6]), .out_18(\output [7]));
  or or_1 (or_1_out, DECREMENT, INCREMENT, Load);
  Adder adder_1 (.a(8'h1), .b(\output ), .out(adder_1_out));  // open: cin, cout
  Subtractor subtractor_1 (.a(\output ), .b(8'h1), .out(subtractor_1_out));  // open: bin, bout

  // Notes on the sheet:
  //   We set up a 4-bit multiplexer
  //   2.bit of mux: increment operation, we add +1 to the data in the output.
  //   3.bit of mux: decrement op. We make -1 from the data in the output.
  //   1.bit of mux: While our input data is load:1, when the clock comes, it loads our input to the registers.
  //   4.bit of mux, if increment and decrement operations come 1 at the same time, we continue to keep the data in the output without making any changes
endmodule
