// Logisim project microhw3.circ as structural Verilog: 15 circuits, main circuit main
module main (
  input  [15:0] INPUT_1,
  input  [15:0] INPUT_2,
  input  in_3,
  input  [11:0] in_4,
  input  [15:0] INPUT_1_2,
  input  [11:0] in_6,
  input  in_7,
  input  in_8,
  output [15:0] out_9
);

  wire and_1_out, and_2_out, and_3_out, and_4_out, and_5_out, and_6_out, and_7_out, and_8_out, and_9_out,
       CLK, INPUT2_out, INTACK, MEMLD, PB_1, PB_2;
  wire [0:0] s_r_ff_1_q, s_r_ff_2_q;
  wire [11:0] ADDRESS_OUT;
  wire [15:0] DATA_IN, DATA_OUT, MEM_OUT, multiplexer_1_out, multiplexer_2_out, multiplexer_4_out,
       multiplexer_5_out, undriven;

  Clock clock_1 (.out(CLK));
  Button button_1 (.out(PB_1));
  Button button_2 (.out(PB_2));
  and and_1 (and_1_out, ~s_r_ff_1_q[0], PB_2);  // AND_Gate
  and and_2 (and_2_out, and_5_out, s_r_ff_1_q[0]);
  S_R_Flip_Flop s_r_ff_1 (.S(and_1_out), .clk(CLK), .R(and_2_out), .Q(s_r_ff_1_q[0]));  // open: Qn, preset, reset, en
  and and_3 (and_3_out, ~s_r_ff_2_q[0], PB_1);  // AND_Gate
  S_R_Flip_Flop s_r_ff_2 (.S(and_3_out), .clk(CLK), .R(and_4_out), .Q(s_r_ff_2_q[0]));  // open: Qn, preset, reset, en
  and and_4 (and_4_out, and_8_out, s_r_ff_2_q[0]);
  and and_5 (and_5_out, ~ADDRESS_OUT[0], INPUT2_out);  // AND_Gate
  and and_6 (and_6_out, ~ADDRESS_OUT[10], ~ADDRESS_OUT[11]);  // AND_Gate
  and and_7 (and_7_out, ~in_7, in_8);  // AND_Gate
  and INPUT2 (INPUT2_out, ADDRESS_OUT[11], ADDRESS_OUT[10], ADDRESS_OUT[9], ADDRESS_OUT[8], ADDRESS_OUT[7], ADDRESS_OUT[6], ADDRESS_OUT[5], ADDRESS_OUT[4], ~ADDRESS_OUT[3], ~ADDRESS_OUT[2], ADDRESS_OUT[1], 1'b1);  // AND_Gate
  and and_8 (and_8_out, ~ADDRESS_OUT[0], and_9_out);  // AND_Gate
  Multiplexer #(.width(16), .enable("false")) multiplexer_1 (
    .in0(INPUT_2), .in1({{15{1'b0}}, s_r_ff_1_q[0]}), .out(multiplexer_1_out), .sel(ADDRESS_OUT[0]));
  Multiplexer #(.width(16), .enable("false")) multiplexer_2 (
    .in0(INPUT_1), .in1({{15{1'b0}}, s_r_ff_2_q[0]}), .out(multiplexer_2_out), .sel(ADDRESS_OUT[0]));
  RAM #(.addrWidth(12), .dataWidth(16), .bus("separate")) ram_1 (
    .addr(ADDRESS_OUT), .din(DATA_OUT), .data(MEM_OUT), .str(MEMLD), .clk(CLK));  // open: sel, ld, clr
  Multiplexer #(.width(16), .enable("false")) multiplexer_3 (.in0(INPUT_1_2), .in1(undriven), .out(out_9), .sel(in_7));
  Multiplexer #(.width(16), .enable("false")) multiplexer_4 (
    .in0({16{1'b0}}), .in1(MEM_OUT), .out(multiplexer_4_out), .sel(and_6_out));
  Multiplexer #(.width(16), .enable("false")) multiplexer_5 (
    .in0(multiplexer_4_out), .in1(multiplexer_1_out), .out(multiplexer_5_out), .sel(INPUT2_out));
  Multiplexer #(.width(16), .enable("false")) multiplexer_6 (
    .in0(multiplexer_5_out), .in1(multiplexer_2_out), .out(DATA_IN), .sel(and_9_out));
  and and_9 (and_9_out, ADDRESS_OUT[11], ADDRESS_OUT[10], ADDRESS_OUT[9], ADDRESS_OUT[8], ADDRESS_OUT[7], ADDRESS_OUT[6], ADDRESS_OUT[5], ADDRESS_OUT[4], ~ADDRESS_OUT[3], ~ADDRESS_OUT[2], ~ADDRESS_OUT[1], 1'b1);  // AND_Gate
  CPU cpu_1 (
    .ADDRESS_BUS(ADDRESS_OUT), .DATA_OUT(DATA_OUT), .DATA_IN(DATA_IN), .out_5(INTACK), .out_6(MEMLD),
    .in_2(in_3));

  // Other names for the same wires on the sheet: PIN_1[15:0] = INPUT_1; PIN_2[15:0] = INPUT_2

  // Notes on the sheet:
  //   0xFF1
  //   0xFF0
endmodule

module alu (
  input  [15:0] Din1,
  input  [15:0] Din2,
  input  [5:0] ALUOP,
  output [15:0] dataout,
  output out_5
);

  wire [15:0] adder_1_out, adder_2_out, and_1_out, multiplexer_1_out, not_1_out, or_1_out, subtractor_1_out,
       subtractor_2_out, xor_1_out;

  Adder #(.width(16)) adder_1 (.a(Din1), .b(Din2), .out(adder_1_out));  // open: cin, cout
  Subtractor #(.width(16)) subtractor_1 (.a(Din1), .b(Din2), .out(subtractor_1_out));  // open: bin, bout
  assign and_1_out = Din1 & Din2;  // AND_Gate and_1, 16 bits wide
  assign or_1_out = Din1 | Din2;  // OR_Gate or_1, 16 bits wide
  assign xor_1_out = Din1 ^ Din2;  // XOR_Gate xor_1, 16 bits wide
  assign not_1_out = ~Din2;  // NOT_Gate not_1, 16 bits wide
  Adder #(.width(16)) adder_2 (.a(Din2), .b(16'h1), .out(adder_2_out));  // open: cin, cout
  Subtractor #(.width(16)) subtractor_2 (.a(Din2), .b(16'h1), .out(subtractor_2_out));  // open: bin, bout
  Multiplexer #(.select(3), .width(16), .enable("false")) multiplexer_1 (
    .in0(not_1_out), .in1(Din2), .in2(adder_2_out), .in3(subtractor_2_out), .out(multiplexer_1_out),
    .sel({1'b0, ALUOP[1:0]}));  // open: in4, in5, in6, in7
  Multiplexer #(.select(3), .width(16), .enable("false")) multiplexer_2 (
    .in0(adder_1_out), .in1(subtractor_1_out), .in2(and_1_out), .in3(or_1_out), .in4(xor_1_out),
    .in7(multiplexer_1_out), .out(dataout), .sel(ALUOP[5:3]));  // open: in5, in6
  nor zeroFlag (out_5, dataout[15], dataout[14], dataout[13], dataout[12], dataout[11], dataout[10], dataout[9], dataout[8], dataout[7], dataout[6], dataout[5], dataout[4], dataout[3], dataout[2], dataout[1], dataout[0]);
endmodule

module _1b_register (
  input  data_in,
  input  clk,
  input  load,
  output data_out
);

  wire not_1_out;

  not not_1 (not_1_out, data_in);
  S_R_Flip_Flop s_r_ff_1 (.S(data_in), .clk(clk), .R(not_1_out), .Q(data_out), .en(load));  // open: Qn, preset, reset
endmodule

module _3b_register (
  input  [2:0] INPUT,
  input  CLK,
  input  LD,
  output [2:0] OUTPUT
);

  _1b_register u_1b_register_1 (.data_in(INPUT[0]), .clk(CLK), .load(LD), .data_out(OUTPUT[0]));
  _1b_register u_1b_register_2 (.data_in(INPUT[1]), .clk(CLK), .load(LD), .data_out(OUTPUT[1]));
  _1b_register u_1b_register_3 (.data_in(INPUT[2]), .clk(CLK), .load(LD), .data_out(OUTPUT[2]));
endmodule

module _4b_register (
  input  [3:0] INPUT,
  input  CLK,
  input  LD,
  output [3:0] OUTPUT
);

  _1b_register u_1b_register_1 (.data_in(INPUT[0]), .clk(CLK), .load(LD), .data_out(OUTPUT[0]));
  _1b_register u_1b_register_2 (.data_in(INPUT[1]), .clk(CLK), .load(LD), .data_out(OUTPUT[1]));
  _1b_register u_1b_register_3 (.data_in(INPUT[2]), .clk(CLK), .load(LD), .data_out(OUTPUT[2]));
  _1b_register u_1b_register_4 (.data_in(INPUT[3]), .clk(CLK), .load(LD), .data_out(OUTPUT[3]));
endmodule

module _12b_register (
  input  [11:0] INPUT,
  input  CLK,
  input  LD,
  output [11:0] OUTPUT
);

  _3b_register u_3b_register_1 (.INPUT(INPUT[2:0]), .CLK(CLK), .LD(LD), .OUTPUT(OUTPUT[2:0]));
  _3b_register u_3b_register_2 (.INPUT(INPUT[5:3]), .CLK(CLK), .LD(LD), .OUTPUT(OUTPUT[5:3]));
  _3b_register u_3b_register_3 (.INPUT(INPUT[8:6]), .CLK(CLK), .LD(LD), .OUTPUT(OUTPUT[8:6]));
  _3b_register u_3b_register_4 (.INPUT(INPUT[11:9]), .CLK(CLK), .LD(LD), .OUTPUT(OUTPUT[11:9]));
endmodule

module _16b_register (
  input  [15:0] INPUT,
  input  CLK,
  input  LD,
  output [15:0] OUTPUT
);

  _4b_register u_4b_register_1 (.INPUT(INPUT[3:0]), .CLK(CLK), .LD(LD), .OUTPUT(OUTPUT[3:0]));
  _4b_register u_4b_register_2 (.INPUT(INPUT[7:4]), .CLK(CLK), .LD(LD), .OUTPUT(OUTPUT[7:4]));
  _4b_register u_4b_register_3 (.INPUT(INPUT[11:8]), .CLK(CLK), .LD(LD), .OUTPUT(OUTPUT[11:8]));
  _4b_register u_4b_register_4 (.INPUT(INPUT[15:12]), .CLK(CLK), .LD(LD), .OUTPUT(OUTPUT[15:12]));
endmodule

module register_bank (
  input  [2:0] RG_SELECT,
  input  RG_LOAD,
  input  [15:0] DATAIN,
  input  SP_plus_plus,
  input  SP_minus_minus,
  output [15:0] DOUT_0,
  output [15:0] DOUT_1,
  output [15:0] DOUT_2,
  output [15:0] DOUT_3,
  output [15:0] DOUT_4,
  output [15:0] DOUT_5,
  output [15:0] DOUT_6,
  output [15:0] DOUT_7
);

  wire and_1_out, and_2_out, and_3_out, and_4_out, and_5_out, and_6_out, and_7_out, and_8_out, clock_1_out,
       decoder_1_out0, decoder_1_out1, decoder_1_out2, decoder_1_out3, decoder_1_out4, decoder_1_out5,
       decoder_1_out6, decoder_1_out7, or_1_out, or_2_out;
  wire [15:0] adder_1_out, multiplexer_1_out, multiplexer_2_out, subtractor_1_out;

  Decoder #(.select(3), .enable("false")) decoder_1 (
    .out0(decoder_1_out0), .out1(decoder_1_out1), .out2(decoder_1_out2), .out3(decoder_1_out3),
    .out4(decoder_1_out4), .out5(decoder_1_out5), .out6(decoder_1_out6), .out7(decoder_1_out7),
    .sel(RG_SELECT));
  and and_1 (and_1_out, decoder_1_out0, RG_LOAD);
  and and_2 (and_2_out, decoder_1_out1, RG_LOAD);
  and and_3 (and_3_out, decoder_1_out2, RG_LOAD);
  and and_4 (and_4_out, decoder_1_out3, RG_LOAD);
  and and_5 (and_5_out, decoder_1_out4, RG_LOAD);
  and and_6 (and_6_out, decoder_1_out5, RG_LOAD);
  and and_7 (and_7_out, decoder_1_out6, RG_LOAD);
  and and_8 (and_8_out, decoder_1_out7, RG_LOAD);
  or or_1 (or_1_out, SP_plus_plus, SP_minus_minus);
  Multiplexer #(.width(16), .enable("false")) multiplexer_1 (
    .in0(DATAIN), .in1(adder_1_out), .out(multiplexer_1_out), .sel(SP_plus_plus));
  Multiplexer #(.width(16), .enable("false")) multiplexer_2 (
    .in0(multiplexer_1_out), .in1(subtractor_1_out), .out(multiplexer_2_out), .sel(SP_minus_minus));
  or or_2 (or_2_out, or_1_out, and_8_out);
  _16b_register u_16b_register_1 (.INPUT(DATAIN), .CLK(clock_1_out), .LD(and_1_out), .OUTPUT(DOUT_0));
  _16b_register u_16b_register_2 (.INPUT(DATAIN), .CLK(clock_1_out), .LD(and_2_out), .OUTPUT(DOUT_1));
  _16b_register u_16b_register_3 (.INPUT(DATAIN), .CLK(clock_1_out), .LD(and_3_out), .OUTPUT(DOUT_2));
  _16b_register u_16b_register_4 (.INPUT(DATAIN), .CLK(clock_1_out), .LD(and_4_out), .OUTPUT(DOUT_3));
  _16b_register u_16b_register_5 (.INPUT(DATAIN), .CLK(clock_1_out), .LD(and_5_out), .OUTPUT(DOUT_4));
  _16b_register u_16b_register_6 (.INPUT(DATAIN), .CLK(clock_1_out), .LD(and_6_out), .OUTPUT(DOUT_5));
  _16b_register u_16b_register_7 (.INPUT(DATAIN), .CLK(clock_1_out), .LD(and_7_out), .OUTPUT(DOUT_6));
  _16b_register u_16b_register_8 (.INPUT(multiplexer_2_out), .CLK(clock_1_out), .LD(or_2_out), .OUTPUT(DOUT_7));
  Clock clock_1 (.out(clock_1_out));
  Adder #(.width(16)) adder_1 (.a(DOUT_7), .b(16'h1), .out(adder_1_out));  // open: cin, cout
  Subtractor #(.width(16)) subtractor_1 (.a(DOUT_7), .b(16'h1), .out(subtractor_1_out));  // open: bin, bout
endmodule

module CPU (
  input  [15:0] DATA_IN,
  input  in_2,
  output [11:0] ADDRESS_BUS,
  output [15:0] DATA_OUT,
  output out_5,
  output out_6
);

  wire alu_1_out_5, clock_1_out, control_unit_1_zfld, control_unit_1_zfpop, INTLD, IRLD, MUX, PCINC, PCLD,
       pcmux, REGLD, SP_minus_minus, SP_plus_plus, zero_flag_1_goes_to_control_unit;
  wire [1:0] ARMUX, datamux;
  wire [2:0] instruction_register_1_ir_2_0, instruction_register_1_ir_5_3, instruction_register_1_ir_6_8;
  wire [5:0] instruction_register_1_ir_6_11;
  wire [11:0] adder_1_out, adder_2_out, bit_extender_1_out, instruction_register_1_ir_out, multiplexer_2_out,
       n12b_register_1_output, n16to12_1_out_2, n16to12_2_out_2, PC_address;
  wire [15:0] alu_1_dataout, multiplexer_4_out, multiplexer_5_out, multiplexer_6_out, register_bank_1_dout_0,
       register_bank_1_dout_1, register_bank_1_dout_2, register_bank_1_dout_3, register_bank_1_dout_4,
       register_bank_1_dout_5, register_bank_1_dout_6, register_bank_1_dout_7, zero_flag_1_goes_to_memory;

  control_unit control_unit_1 (
    .INT(in_2), .ZF(zero_flag_1_goes_to_control_unit), .SP_minus_minus(SP_minus_minus), .IRLD(IRLD),
    .MUX(MUX), .REGLD(REGLD), .PCLD(PCLD), .ZFLD(control_unit_1_zfld), .PCINC(PCINC), .ARMUX(ARMUX),
    .MEMLD(out_6), .opcode(DATA_IN[15:12]), .DATAMUX(datamux), .PCMUX(pcmux), .SP_plus_plus(SP_plus_plus),
    .INTACK(out_5), .ZFPOP(control_unit_1_zfpop), .INTLD(INTLD));
  Clock clock_1 (.out(clock_1_out));
  Adder #(.width(12)) adder_1 (.a(bit_extender_1_out), .b(12'h7f0), .out(adder_1_out));  // open: cin, cout
  _12b_register u_12b_register_1 (.INPUT(adder_1_out), .CLK(clock_1_out), .LD(INTLD), .OUTPUT(n12b_register_1_output));
  assign bit_extender_1_out = {{9{1'b0}}, DATA_IN[2:0]};  // Bit_Extender bit_extender_1
  Multiplexer #(.select(2), .width(12), .enable("false")) multiplexer_1 (
    .in0(PC_address), .in1(n16to12_1_out_2), .in2(n16to12_2_out_2), .in3(n12b_register_1_output),
    .out(ADDRESS_BUS), .sel(ARMUX));
  PC PC (.INPUT(multiplexer_2_out), .PCINC(PCINC), .PCLD(PCLD), .ADDRESS(PC_address));
  Multiplexer #(.width(12), .enable("false")) multiplexer_2 (
    .in0(adder_2_out), .in1(instruction_register_1_ir_out), .out(multiplexer_2_out), .sel(pcmux));
  Adder #(.width(12)) adder_2 (
    .a(PC_address), .b(instruction_register_1_ir_out), .out(adder_2_out));  // open: cin, cout
  register_bank register_bank_1 (
    .RG_SELECT(instruction_register_1_ir_2_0), .RG_LOAD(REGLD), .DATAIN(multiplexer_5_out),
    .DOUT_0(register_bank_1_dout_0), .DOUT_1(register_bank_1_dout_1), .DOUT_2(register_bank_1_dout_2),
    .DOUT_3(register_bank_1_dout_3), .DOUT_4(register_bank_1_dout_4), .DOUT_5(register_bank_1_dout_5),
    .DOUT_6(register_bank_1_dout_6), .DOUT_7(register_bank_1_dout_7), .SP_plus_plus(SP_plus_plus),
    .SP_minus_minus(SP_minus_minus));
  Multiplexer #(.select(2), .width(16), .enable("false")) multiplexer_3 (
    .in0(multiplexer_4_out), .in1({4'b0000, PC_address}), .in2(zero_flag_1_goes_to_memory), .out(DATA_OUT),
    .sel(datamux));  // open: in3
  Multiplexer #(.select(3), .width(16), .enable("false")) multiplexer_4 (
    .in0(register_bank_1_dout_0), .in1(register_bank_1_dout_1), .in2(register_bank_1_dout_2),
    .in3(register_bank_1_dout_3), .in4(register_bank_1_dout_4), .in5(register_bank_1_dout_5),
    .in6(register_bank_1_dout_6), .in7(register_bank_1_dout_7), .out(multiplexer_4_out),
    .sel(instruction_register_1_ir_6_8));
  zero_flag zero_flag_1 (
    .D_0(DATA_IN[0]), .ZF(alu_1_out_5), .GOES_TO_MEMORY(zero_flag_1_goes_to_memory),
    .ZFPOP(control_unit_1_zfpop), .ZFLD(control_unit_1_zfld),
    .GOES_TO_CONTROL_UNIT(zero_flag_1_goes_to_control_unit));
  Multiplexer #(.width(16), .enable("false")) multiplexer_5 (
    .in0(alu_1_dataout), .in1(DATA_IN), .out(multiplexer_5_out), .sel(MUX));
  _16to12 u_16to12_1 (.in_1(multiplexer_6_out), .out_2(n16to12_1_out_2));
  _16to12 u_16to12_2 (.in_1(register_bank_1_dout_7), .out_2(n16to12_2_out_2));
  Multiplexer #(.select(3), .width(16), .enable("false")) multiplexer_6 (
    .in0(register_bank_1_dout_0), .in1(register_bank_1_dout_1), .in2(register_bank_1_dout_2),
    .in3(register_bank_1_dout_3), .in4(register_bank_1_dout_4), .in5(register_bank_1_dout_5),
    .in6(register_bank_1_dout_6), .in7(register_bank_1_dout_7), .out(multiplexer_6_out),
    .sel(instruction_register_1_ir_5_3));
  alu alu_1 (
    .Din1(multiplexer_4_out), .Din2(multiplexer_6_out), .dataout(alu_1_dataout), .out_5(alu_1_out_5),
    .ALUOP(instruction_register_1_ir_6_11));
  instruction_register instruction_register_1 (
    .IR_IN(DATA_IN[11:0]), .IR_OUT(instruction_register_1_ir_out), .IR_LD(IRLD),
    .IR_2_0(instruction_register_1_ir_2_0), .IR_5_3(instruction_register_1_ir_5_3),
    .IR_6_8(instruction_register_1_ir_6_8), .IR_6_11(instruction_register_1_ir_6_11));

  // Other names for the same wires on the sheet: INTACK = out_5; MEMLD = out_6
endmodule

module instruction_register (
  input  [11:0] IR_IN,
  input  IR_LD,
  output [11:0] IR_OUT,
  output [2:0] IR_2_0,
  output [2:0] IR_5_3,
  output [2:0] IR_6_8,
  output [5:0] IR_6_11
);

  wire clock_1_out;

  Clock clock_1 (.out(clock_1_out));
  _12b_register u_12b_register_1 (
    .INPUT(IR_IN), .CLK(clock_1_out), .LD(IR_LD), .OUTPUT({IR_6_11[5:3], IR_6_8, IR_5_3, IR_2_0}));

  assign IR_6_11[2:0] = IR_6_8;
  assign IR_OUT = {IR_6_11[5:3], IR_6_8, IR_5_3, IR_2_0};
endmodule

module zero_flag (
  input  ZFPOP,
  input  D_0,
  input  ZF,
  input  ZFLD,
  output [15:0] GOES_TO_MEMORY,
  output GOES_TO_CONTROL_UNIT
);

  wire and_1_out, and_2_out, and_3_out, and_4_out, clock_1_out, not_1_out, not_2_out, or_1_out, or_2_out;

  and and_1 (and_1_out, D_0, ZFPOP);
  and and_2 (and_2_out, ZF, ZFLD);
  not not_1 (not_1_out, D_0);
  and and_3 (and_3_out, not_1_out, ZFPOP);
  not not_2 (not_2_out, ZF);
  and and_4 (and_4_out, not_2_out, ZFLD);
  or or_1 (or_1_out, and_1_out, and_2_out);
  or or_2 (or_2_out, and_3_out, and_4_out);
  Clock clock_1 (.out(clock_1_out));
  S_R_Flip_Flop s_r_ff_1 (
    .S(or_1_out), .clk(clock_1_out), .R(or_2_out), .Q(GOES_TO_CONTROL_UNIT));  // open: Qn, preset, reset, en
  assign GOES_TO_MEMORY = {{15{1'b0}}, GOES_TO_CONTROL_UNIT};  // Bit_Extender bit_extender_1
endmodule

module _16to12 (
  input  [15:0] in_1,
  output [11:0] out_2
);


  assign out_2 = in_1[11:0];
endmodule

module PC (
  input  [11:0] INPUT,
  input  PCINC,
  input  PCLD,
  output [11:0] ADDRESS
);

  wire clock_1_out, or_1_out;
  wire [11:0] adder_1_out, multiplexer_1_out;

  Adder #(.width(12)) adder_1 (.a(ADDRESS), .b(12'h1), .out(adder_1_out));  // open: cin, cout
  or or_1 (or_1_out, PCINC, PCLD);
  Multiplexer #(.width(12), .enable("false")) multiplexer_1 (
    .in0(INPUT), .in1(adder_1_out), .out(multiplexer_1_out), .sel(PCINC));
  Clock clock_1 (.out(clock_1_out));
  _12b_register u_12b_register_1 (.INPUT(multiplexer_1_out), .CLK(clock_1_out), .LD(or_1_out), .OUTPUT(ADDRESS));
endmodule

module _5b_register (
  input  [4:0] in_1,
  input  LD,
  input  CLK,
  output [4:0] out
);

  _1b_register u_1b_register_1 (.data_in(in_1[0]), .clk(CLK), .load(LD), .data_out(out[0]));
  _1b_register u_1b_register_2 (.data_in(in_1[1]), .clk(CLK), .load(LD), .data_out(out[1]));
  _1b_register u_1b_register_3 (.data_in(in_1[2]), .clk(CLK), .load(LD), .data_out(out[2]));
  _1b_register u_1b_register_4 (.data_in(in_1[3]), .clk(CLK), .load(LD), .data_out(out[3]));
  _1b_register u_1b_register_5 (.data_in(in_1[4]), .clk(CLK), .load(LD), .data_out(out[4]));
endmodule

module control_unit (
  input  INT,
  input  [3:0] opcode,
  input  ZF,
  output IRLD,
  output MEMLD,
  output MUX,
  output ZFLD,
  output REGLD,
  output [1:0] ARMUX,
  output PCINC,
  output PCLD,
  output [1:0] DATAMUX,
  output SP_minus_minus,
  output SP_plus_plus,
  output PCMUX,
  output INTLD,
  output INTACK,
  output ZFPOP
);

  wire and_2_out, and_3_out, clock_1_out, s_r_ff_1_q;
  wire [1:1] and_1_out;
  wire [3:0] multiplexer_1_out;
  wire [4:0] multiplexer_2_out, multiplexer_3_out, n5b_register_1_out;
  wire [24:0] rom_1_data;

  and and_1 (and_1_out[1], ~opcode[0], ~opcode[1], opcode[2], ~opcode[3]);  // AND_Gate
  Multiplexer #(.select(2), .width(4), .disabled(0), .enable("false")) multiplexer_1 (
    .in0(opcode), .in1(opcode), .in2(4'b0000), .in3(4'b0101), .out(multiplexer_1_out),
    .sel({and_1_out[1], ZF}));
  Multiplexer #(.width(5), .enable("false")) multiplexer_2 (
    .in0(rom_1_data[4:0]), .in1({1'b0, multiplexer_1_out}), .out(multiplexer_2_out), .sel(rom_1_data[24]));
  Multiplexer #(.width(5), .enable("false")) multiplexer_3 (
    .in0(multiplexer_2_out), .in1(5'b10011), .out(multiplexer_3_out), .sel(and_2_out));
  Clock clock_1 (.out(clock_1_out));
  and and_2 (and_2_out, INT, s_r_ff_1_q, and_3_out);
  _5b_register u_5b_register_1 (.in_1(multiplexer_3_out), .LD(1'b1), .CLK(clock_1_out), .out(n5b_register_1_out));
  ROM #(.addrWidth(5), .dataWidth(25)) rom_1 (
    .addr(n5b_register_1_out),
    .data({rom_1_data[24], ZFPOP, INTACK, INTLD, rom_1_data[20:19], DATAMUX, PCMUX, SP_plus_plus, SP_minus_minus, PCLD, PCINC, ARMUX, REGLD, ZFLD, MUX, MEMLD, IRLD, rom_1_data[4:0]}));  // open: sel
  and and_3 (and_3_out, ~rom_1_data[0], ~rom_1_data[1], ~rom_1_data[2], ~rom_1_data[3], ~rom_1_data[4]);  // AND_Gate
  S_R_Flip_Flop s_r_ff_1 (.S(rom_1_data[19]), .R(rom_1_data[20]), .Q(s_r_ff_1_q));  // open: clk, Qn, preset, reset, en

  // Notes on the sheet:
  //   contents of rom_1 (hex, n*v repeats v):
  //   100103f 1280 680 440 0 2000 0 300 4840 8011 24845 8012 80000 100000 800f 808890 12800 a80 12880
  //   124854 644855 12c00
endmodule
